# Fritzing sketch Untitled Sketch (saved by Fritzing 0.9.3b)
breadboards: 1

parts:
  R1 = Resistor [tolerance=±5% resistance=220 package=THT]
  R2 = Resistor [tolerance=±5% resistance=220 package=THT]
  LED1 = LED - 5mm [color="Red (633nm)" package="5 mm [THT]"]
  LED2 = LED - 5mm [color="Red (633nm)" package="5 mm [THT]"]
  LED3 = LED - 5mm [color="Red (633nm)" package="5 mm [THT]"]
  LED4 = LED - 5mm [color="Red (633nm)" package="5 mm [THT]"]
  R3 = Resistor [tolerance=±5% resistance=220 package=THT]
  R4 = Resistor [tolerance=±5% resistance=220 package=THT]
  LED5 = LED - 5mm [color="Red (633nm)" package="5 mm [THT]"]  # not connected
  R5 = Resistor [tolerance=±5% resistance=220 package=THT]
  R6 = Resistor [tolerance=±5% resistance=220 package=THT]
  R7 = Resistor [tolerance=±5% resistance=220 package=THT]
  R8 = Resistor [tolerance=±5% resistance=220 package=THT]
  R9 = Resistor [tolerance=±5% resistance=220 package=THT]
  R10 = Resistor [tolerance=±5% resistance=220 package=THT]
  LED6 = LED - 5mm [color="Red (633nm)" package="5 mm [THT]"]
  LED7 = LED - 5mm [color="Red (633nm)" package="5 mm [THT]"]
  LED8 = LED - 5mm [color="Red (633nm)" package="5 mm [THT]"]
  LED9 = LED - 5mm [color="Red (633nm)" package="5 mm [THT]"]
  LED10 = LED - 5mm [color="Red (633nm)" package="5 mm [THT]"]
  Composant1 = Arduino Uno (Rev3)

nets:
  N1: R1.Pin_0, LED1.cathode
  N2: R1.Pin_1, Composant1.D9_PWM
  N3: R2.Pin_0, LED3.cathode
  N4: R2.Pin_1, Composant1.D8
  N5: LED1.anode, LED2.anode, LED3.anode, LED4.anode, LED6.anode, LED7.anode, LED8.anode, LED9.anode, LED10.cathode, Composant1.GND
  N6: LED2.cathode, R5.Pin_0
  N7: LED4.cathode, R3.Pin_1
  N8: R3.Pin_0, Composant1.D10_PWM/SS
  N9: R4.Pin_0, Composant1.D11_PWM/MOSI
  N10: R5.Pin_1, Composant1.D7
  N11: R6.Pin_0, LED6.cathode
  N12: R6.Pin_1, Composant1.D6_PWM
  N13: R7.Pin_0, LED7.cathode
  N14: R7.Pin_1, Composant1.D5_PWM
  N15: R8.Pin_0, LED8.cathode
  N16: R8.Pin_1, Composant1.D4
  N17: R9.Pin_1, LED10.anode, Composant1.D3_PWM
  N18: R10.Pin_0, Composant1.D2
  N19: R10.Pin_1, LED9.cathode
