# Fritzing sketch circuit (saved by Fritzing 0.9.3b)
breadboards: 1

parts:
  R1 = Resistor [tolerance=±5% resistance=220 package=THT]
  LED1 = LED - 5mm [color="Red (633nm)" package="5 mm [THT]"]
  R2 = Resistor [tolerance=±5% resistance=220 package=THT]
  C1 = Electrolytic Capacitor [capacitance=1µF package="100 mil [THT, electrolytic]"]
  C2 = Tantalum Capacitor [capacitance=1μF package="100 mil [THT, tantalum]"]
  R3 = Resistor [tolerance=±5% resistance=220 package=THT]
  U2 = LM124-324 Quad Opamp [package="DIP (Dual Inline)"]
  R4 = Resistor [tolerance=±5% resistance=220 package=THT]
  C3 = Ceramic Capacitor [capacitance=100nF package="100 mil [THT, multilayer]"]
  C4 = Electrolytic Capacitor [capacitance=1µF package="100 mil [THT, electrolytic]"]
  R5 = Resistor [tolerance=±5% resistance=220 package=THT]
  R6 = Resistor [tolerance=±5% resistance=220 package=THT]
  C5 = Ceramic Capacitor [capacitance=100nF package="100 mil [THT, multilayer]"]
  R7 = Resistor [tolerance=±5% resistance=220 package=THT]
  Q1 = NPN-Transistor [package="TO92 [THT]"]
  R8 = Resistor [tolerance=±5% resistance=220 package=THT]
  Composant1 = Arduino Uno (Rev3)

nets:
  N1: R1.Pin_0, LED1.anode
  N2: R1.Pin_1, R2.Pin_1, U2.VCC-, Q1.C, Composant1.5V
  N3: LED1.cathode, C2.-, R3.Pin_0, U2.VCC+, R4.Pin_1, R5.Pin_0, R8.Pin_0, Composant1.GND
  N4: R2.Pin_0, C1.-, C2.+
  N5: C1.+, R3.Pin_1, U2.3IN+
  N6: U2.2IN+, C4.+, R8.Pin_1
  N7: U2.2IN-, R5.Pin_1, R6.Pin_0, C5.0
  N8: U2.2OUT, R6.Pin_1, C5.1, R7.Pin_0
  N9: U2.3OUT, C3.1, C4.-
  N10: U2.3IN-, R4.Pin_0, C3.0
  N11: R7.Pin_1, Q1.B
