# Fritzing sketch circuit_module 1 (saved by Fritzing 0.9.3b)
breadboards: 1

parts:
  Composant1 = Arduino Uno (Rev3)
  LED1 = LED - 5mm [color="Infrared (880nm)" package="5 mm [THT]"]
  Q1 = LTR-301 [package=ltr-301]
  C1 = Tantalum Capacitor [capacitance=1μF package="100 mil [THT, tantalum]"]
  R1 = Resistor [tolerance=±5% resistance=220 package=THT]
  R2 = Resistor [tolerance=±5% resistance=220 package=THT]
  U1 = LM124-324 Quad Opamp [package="DIP (Dual Inline)"]
  R3 = Resistor [tolerance=±5% resistance=220 package=THT]
  C2 = Ceramic Capacitor [capacitance=100nF package="100 mil [THT, multilayer]"]
  C3 = Ceramic Capacitor [capacitance=100nF package="100 mil [THT, multilayer]"]
  R4 = Resistor [tolerance=±5% resistance=220 package=THT]
  R5 = Resistor [tolerance=±5% resistance=220 package=THT]
  C4 = Tantalum Capacitor [capacitance=1μF package="100 mil [THT, tantalum]"]
  R6 = Resistor [tolerance=±5% resistance=220 package=THT]
  Q2 = PNP-Transistor [package="TO92 [THT]"]
  R7 = Resistor [tolerance=±5% resistance=220 package=THT]

nets:
  N1: Composant1.A0, Q2.E
  N2: Composant1.5V, C1.+, R2.Pin_0, U1.VCC+, U1.VCC-, R3.Pin_1, R4.Pin_0, R4.Pin_1, R5.Pin_1, C4.-
  N3: Composant1.GND, R1.Pin_1, U1.4OUT
  N4: LED1.anode, Q1.C, R2.Pin_1, U1.1IN+
  N5: Q1.E, C1.-, R1.Pin_0
  N6: U1.1OUT, C2.1, C4.+
  N7: U1.1IN-, R3.Pin_0, C2.0
  N8: U1.4IN+, R7.Pin_0
  N9: U1.4IN-, C3.0, R6.Pin_0
  N10: C3.1, R5.Pin_0
